// Logisim project p3.circ as structural Verilog: 1 circuit, main circuit main
module main (
  input  in_1,
  input  in_2
);

  wire AUR, CLCK, CTRLW, decoder_1_out0, decoder_1_out1, decoder_1_out2, decoder_1_out3, decoder_1_out4,
       decoder_1_out5, decoder_1_out6, decoder_1_out7, LIR;
  wire [14:0] ALU;
  wire [15:0] A, B, R0_q, R1_q, R2_q, R3_q, R4_q, R5_q, R6_q, R7_q;

  Clock clock_1 (.out(CLCK));
  ROM #(.dataWidth(16)) rom_1 (.data({ALU, CTRLW}));  // open: addr
  // Probe on 3'b011
  // Probe on A
  Decoder #(.enable("false"), .select(3)) decoder_1 (
    .out0(decoder_1_out0), .out1(decoder_1_out1), .out2(decoder_1_out2), .out3(decoder_1_out3),
    .out4(decoder_1_out4), .out5(decoder_1_out5), .out6(decoder_1_out6), .out7(decoder_1_out7), .sel(3'b011));
  Register #(.width(16)) R7 (.D(16'hf223), .en(decoder_1_out7), .clk(CLCK), .Q(R7_q), .clr(in_2));
  Register #(.width(16)) R6 (.D(16'hf223), .en(decoder_1_out6), .clk(CLCK), .Q(R6_q), .clr(in_2));
  Register #(.width(16)) R5 (.D(16'hf223), .en(decoder_1_out5), .clk(CLCK), .Q(R5_q), .clr(in_2));
  Register #(.width(16)) R4 (.D(16'hf223), .en(decoder_1_out4), .clk(CLCK), .Q(R4_q), .clr(in_2));
  Multiplexer multiplexer_1 (.in0(AUR), .in1(LIR), .sel(CTRLW));  // open: out
  Multiplexer #(.select(3), .width(16)) multiplexer_2 (
    .in0(R0_q), .in1(R1_q), .in2(R2_q), .in3(R3_q), .in4(R4_q), .in5(R5_q), .in6(R6_q), .in7(R7_q), .out(A),
    .sel(ALU[2:0]));
  Register #(.width(16)) R3 (.D(16'hf223), .en(decoder_1_out3), .clk(CLCK), .Q(R3_q), .clr(in_2));
  Register #(.width(16)) R2 (.D(16'hf223), .en(decoder_1_out2), .clk(CLCK), .Q(R2_q), .clr(in_2));
  Register #(.width(16)) R1 (.D(16'hf223), .en(decoder_1_out1), .clk(CLCK), .Q(R1_q), .clr(in_2));
  Multiplexer #(.select(3), .width(16)) multiplexer_3 (
    .in0(R0_q), .in1(R1_q), .in2(R2_q), .in3(R3_q), .in4(R4_q), .in5(R5_q), .in6(R6_q), .in7(R7_q), .out(B),
    .sel(ALU[7:5]));
  Register #(.width(16)) R0 (.D(16'hf223), .en(decoder_1_out0), .clk(CLCK), .Q(R0_q), .clr(in_2));
  // Probe on A
  // also tied to GND on the sheet: ALU[2]
  // also tied to VCC on the sheet: {ALU[0], ALU[1]}

  // Other names for the same wires on the sheet: AU[14:0] = ALU; func2[1:0] = ALU[4:3]; LI[14:0] = ALU;
  //   SELA[2:0] = ALU[2:0]; SELB[2:0] = ALU[7:5]
endmodule
